// Logisim project vpu.circ as structural Verilog: 6 circuits, main circuit VPU
module VPU (
  input  in_1,
  input  [5:0] in_2,
  input  [4:0] in_3,
  input  [4:0] in_4,
  input  [31:0] in_5,
  input  [31:0] in_6,
  input  [23:0] in_7,
  output [31:0] VRegOutHi,
  output [31:0] VRegOutLo,
  output VBus32,
  output VBus64,
  output VPUError
);

  VReg VReg ();  // open: clk, RAMOutHi, RAMOutLo, WEn, out_11, out_13, out_10, out_12, vlen, num16, in_6, vrd, vrs
  VRegCtrl VRegCtrl ();  // open: vop, _16bitRegs, vlen, cfg

  assign VBus32 = 1'b0;
  assign VBus64 = 1'b0;
  assign VPUError = 1'b0;

  // Other names for the same wires on the sheet: CLK = in_1; RAMOutHi[31:0] = in_5; RAMOutLo[31:0] = in_6;
  //   RegOut2[23:0] = in_7; vop[5:0] = in_2; vrd[4:0] = in_3; vrs[4:0] = in_4
endmodule

module VRegRow (
  input  [31:0] RAMOutHi,
  input  [31:0] RAMOutLo,
  input  [3:0] RegEn,
  input  RowEn,
  input  clk,
  output [31:0] OutHi,
  output [31:0] OutLo
);

  wire [0:0] bitadder_1_out;
  wire [1:0] RAMSel;
  wire [3:0] and_1_out;
  wire [7:0] multiplexer_1_out, multiplexer_2_out, multiplexer_3_out, multiplexer_4_out, multiplexer_5_out,
       multiplexer_6_out;

  Register register_1 (.D(RAMOutHi[31:24]), .en(and_1_out[0]), .Q(OutHi[31:24]), .clk(clk));  // open: clr
  Multiplexer #(.select(2), .width(8), .enable("false")) multiplexer_1 (
    .in0(RAMOutHi[31:24]), .in1(RAMOutHi[15:8]), .in2(RAMOutHi[15:8]), .out(multiplexer_1_out), .sel(RAMSel));  // open: in3
  Register register_2 (.D(RAMOutHi[23:16]), .en(and_1_out[0]), .Q(OutHi[23:16]), .clk(clk));  // open: clr
  Register register_3 (.D(multiplexer_1_out), .en(and_1_out[1]), .Q(OutHi[15:8]), .clk(clk));  // open: clr
  Multiplexer #(.select(2), .width(8), .enable("false")) multiplexer_2 (
    .in0(RAMOutHi[23:16]), .in1(RAMOutHi[7:0]), .in2(RAMOutHi[7:0]), .out(multiplexer_2_out), .sel(RAMSel));  // open: in3
  Register register_4 (.D(multiplexer_2_out), .en(and_1_out[1]), .Q(OutHi[7:0]), .clk(clk));  // open: clr
  Multiplexer #(.select(2), .width(8), .enable("false")) multiplexer_3 (
    .in0(RAMOutHi[15:8]), .in1(RAMOutHi[31:24]), .in2(RAMOutLo[31:24]), .out(multiplexer_3_out), .sel(RAMSel));  // open: in3
  Register register_5 (.D(multiplexer_3_out), .en(and_1_out[2]), .Q(OutLo[31:24]), .clk(clk));  // open: clr
  Multiplexer #(.select(2), .width(8), .enable("false")) multiplexer_4 (
    .in0(RAMOutHi[7:0]), .in1(RAMOutHi[23:16]), .in2(RAMOutLo[23:16]), .out(multiplexer_4_out), .sel(RAMSel));  // open: in3
  Register register_6 (.D(multiplexer_4_out), .en(and_1_out[2]), .Q(OutLo[23:16]), .clk(clk));  // open: clr
  Multiplexer #(.select(2), .width(8), .enable("false")) multiplexer_5 (
    .in0(RAMOutHi[31:24]), .in1(RAMOutHi[15:8]), .in2(RAMOutLo[15:8]), .out(multiplexer_5_out), .sel(RAMSel));  // open: in3
  Register register_7 (.D(multiplexer_5_out), .en(and_1_out[3]), .Q(OutLo[15:8]), .clk(clk));  // open: clr
  Multiplexer #(.select(2), .width(8), .enable("false")) multiplexer_6 (
    .in0(RAMOutHi[23:16]), .in1(RAMOutHi[7:0]), .in2(RAMOutLo[7:0]), .out(multiplexer_6_out), .sel(RAMSel));  // open: in3
  Register register_8 (.D(multiplexer_6_out), .en(and_1_out[3]), .Q(OutLo[7:0]), .clk(clk));  // open: clr
  assign and_1_out = RegEn & {4{RowEn}};  // AND_Gate and_1, 4 bits wide
  BitAdder #(.width(4)) bitadder_1 (.in0(RegEn), .out({RAMSel, bitadder_1_out[0]}));

  // Other names for the same wires on the sheet: hi[31:0] = RAMOutHi; lo[31:0] = RAMOutLo; reg3[7:0] = OutHi[7:0];
  //   reg2[7:0] = OutHi[15:8]; reg1[7:0] = OutHi[23:16]; reg0[7:0] = OutHi[31:24]; reg7[7:0] = OutLo[7:0];
  //   reg6[7:0] = OutLo[15:8]; reg5[7:0] = OutLo[23:16]; reg4[7:0] = OutLo[31:24]
endmodule

module VReg (
  input  clk,
  input  WEn,
  input  [31:0] RAMOutHi,
  input  [31:0] RAMOutLo,
  input  [4:0] num16,
  input  in_6,
  input  [4:0] vrd,
  input  [2:0] vlen,
  input  [4:0] vrs,
  output [31:0] out_10,
  output [31:0] out_11,
  output [31:0] out_12,
  output [31:0] out_13
);

  wire demultiplexer_1_out0, demultiplexer_1_out1, demultiplexer_1_out2, demultiplexer_1_out3,
       demultiplexer_1_out4, demultiplexer_1_out5, demultiplexer_1_out6, demultiplexer_1_out7,
       demultiplexer_2_out0, demultiplexer_2_out1, demultiplexer_2_out2, demultiplexer_2_out3,
       demultiplexer_2_out4, demultiplexer_2_out5, demultiplexer_2_out6, demultiplexer_2_out7, not_1_out;
  wire [2:0] vlen_t;
  wire [3:0] RegSel1, RegSel2, RowSel1, RowSel2;
  wire [4:0] num16_t;
  wire [31:0] r00H, r00L, r01H, r01L, r02H, r02L, r03H, r03L, r04H, r04L, r05H, r05L, r06H, r06L, r07H, r07L,
       r08H, r08L, r09H, r09L, r10H, r10L, r11H, r11L, r12H, r12L, r13H, r13L, r14H, r14L, r15H, r15L;

  VRegRow vregrow_1 (
    .clk(clk), .RAMOutHi(RAMOutHi), .RAMOutLo(RAMOutLo), .OutHi(r00H), .OutLo(r00L),
    .RowEn(demultiplexer_1_out0), .RegEn(RegSel1));
  VRegRow vregrow_2 (
    .clk(clk), .RAMOutHi(RAMOutHi), .RAMOutLo(RAMOutLo), .OutHi(r01H), .OutLo(r01L),
    .RowEn(demultiplexer_1_out1), .RegEn(RegSel1));
  VRegRow vregrow_3 (
    .clk(clk), .RAMOutHi(RAMOutHi), .RAMOutLo(RAMOutLo), .OutHi(r02H), .OutLo(r02L),
    .RowEn(demultiplexer_1_out2), .RegEn(RegSel1));
  VRegRow vregrow_4 (
    .clk(clk), .RAMOutHi(RAMOutHi), .RAMOutLo(RAMOutLo), .OutHi(r03H), .OutLo(r03L),
    .RowEn(demultiplexer_1_out3), .RegEn(RegSel1));
  VRegRow vregrow_5 (
    .clk(clk), .RAMOutHi(RAMOutHi), .RAMOutLo(RAMOutLo), .OutHi(r04H), .OutLo(r04L),
    .RowEn(demultiplexer_1_out4), .RegEn(RegSel1));
  VRegRow vregrow_6 (
    .clk(clk), .RAMOutHi(RAMOutHi), .RAMOutLo(RAMOutLo), .OutHi(r05H), .OutLo(r05L),
    .RowEn(demultiplexer_1_out5), .RegEn(RegSel1));
  VRegRow vregrow_7 (
    .clk(clk), .RAMOutHi(RAMOutHi), .RAMOutLo(RAMOutLo), .OutHi(r06H), .OutLo(r06L),
    .RowEn(demultiplexer_1_out6), .RegEn(RegSel1));
  VRegRow vregrow_8 (
    .clk(clk), .RAMOutHi(RAMOutHi), .RAMOutLo(RAMOutLo), .OutHi(r07H), .OutLo(r07L),
    .RowEn(demultiplexer_1_out7), .RegEn(RegSel1));
  Demultiplexer #(.select(3)) demultiplexer_1 (
    .out0(demultiplexer_1_out0), .out1(demultiplexer_1_out1), .out2(demultiplexer_1_out2),
    .out3(demultiplexer_1_out3), .out4(demultiplexer_1_out4), .out5(demultiplexer_1_out5),
    .out6(demultiplexer_1_out6), .out7(demultiplexer_1_out7), .in(WEn), .sel(RowSel1[2:0]), .en(not_1_out));
  not not_1 (not_1_out, RowSel1[3]);
  VRegRow vregrow_9 (
    .clk(clk), .RAMOutHi(RAMOutHi), .RAMOutLo(RAMOutLo), .OutHi(r08H), .OutLo(r08L),
    .RowEn(demultiplexer_2_out0), .RegEn(RegSel1));
  VRegRow vregrow_10 (
    .clk(clk), .RAMOutHi(RAMOutHi), .RAMOutLo(RAMOutLo), .OutHi(r09H), .OutLo(r09L),
    .RowEn(demultiplexer_2_out1), .RegEn(RegSel1));
  VRegRow vregrow_11 (
    .clk(clk), .RAMOutHi(RAMOutHi), .RAMOutLo(RAMOutLo), .OutHi(r10H), .OutLo(r10L),
    .RowEn(demultiplexer_2_out2), .RegEn(RegSel1));
  VRegRow vregrow_12 (
    .clk(clk), .RAMOutHi(RAMOutHi), .RAMOutLo(RAMOutLo), .OutHi(r11H), .OutLo(r11L),
    .RowEn(demultiplexer_2_out3), .RegEn(RegSel1));
  VRegRow vregrow_13 (
    .clk(clk), .RAMOutHi(RAMOutHi), .RAMOutLo(RAMOutLo), .OutHi(r12H), .OutLo(r12L),
    .RowEn(demultiplexer_2_out4), .RegEn(RegSel1));
  VRegRow vregrow_14 (
    .clk(clk), .RAMOutHi(RAMOutHi), .RAMOutLo(RAMOutLo), .OutHi(r13H), .OutLo(r13L),
    .RowEn(demultiplexer_2_out5), .RegEn(RegSel1));
  VRegRow vregrow_15 (
    .clk(clk), .RAMOutHi(RAMOutHi), .RAMOutLo(RAMOutLo), .OutHi(r14H), .OutLo(r14L),
    .RowEn(demultiplexer_2_out6), .RegEn(RegSel1));
  VRegRow vregrow_16 (
    .clk(clk), .RAMOutHi(RAMOutHi), .RAMOutLo(RAMOutLo), .OutHi(r15H), .OutLo(r15L),
    .RowEn(demultiplexer_2_out7), .RegEn(RegSel1));
  Demultiplexer #(.select(3)) demultiplexer_2 (
    .out0(demultiplexer_2_out0), .out1(demultiplexer_2_out1), .out2(demultiplexer_2_out2),
    .out3(demultiplexer_2_out3), .out4(demultiplexer_2_out4), .out5(demultiplexer_2_out5),
    .out6(demultiplexer_2_out6), .out7(demultiplexer_2_out7), .in(WEn), .sel(RowSel1[2:0]), .en(RowSel1[3]));
  Multiplexer #(.select(4), .width(32), .enable("false")) multiplexer_1 (
    .in0(r00H), .in1(r01H), .in2(r02H), .in3(r03H), .in4(r04H), .in5(r05H), .in6(r06H), .in7(r07H),
    .in8(r08H), .in9(r09H), .in10(r10H), .in11(r11H), .in12(r12H), .in13(r13H), .in14(r14H), .in15(r15H),
    .out(out_10), .sel(RowSel1));
  Multiplexer #(.select(4), .width(32), .enable("false")) multiplexer_2 (
    .in0(r00L), .in1(r01L), .in2(r02L), .in3(r03L), .in4(r04L), .in5(r05L), .in6(r06L), .in7(r07L),
    .in8(r08L), .in9(r09L), .in10(r10L), .in11(r11L), .in12(r12L), .in13(r13L), .in14(r14L), .in15(r15L),
    .out(out_12), .sel(RowSel1));
  VTC vtc_1 (.vlen(vlen_t), .num16(num16_t), .VirtAddr(vrd), .PA({RowSel1, RegSel1}));
  VTC vtc_2 (.vlen(vlen_t), .num16(num16_t), .VirtAddr(vrs), .PA({RowSel2, RegSel2}));
  Multiplexer #(.select(4), .width(32), .enable("false")) multiplexer_3 (
    .in0(r00H), .in1(r01H), .in2(r02H), .in3(r03H), .in4(r04H), .in5(r05H), .in6(r06H), .in7(r07H),
    .in8(r08H), .in9(r09H), .in10(r10H), .in11(r11H), .in12(r12H), .in13(r13H), .in14(r14H), .in15(r15H),
    .out(out_11), .sel(RowSel2));
  Multiplexer #(.select(4), .width(32), .enable("false")) multiplexer_4 (
    .in0(r00L), .in1(r01L), .in2(r02L), .in3(r03L), .in4(r04L), .in5(r05L), .in6(r06L), .in7(r07L),
    .in8(r08L), .in9(r09L), .in10(r10L), .in11(r11L), .in12(r12L), .in13(r13L), .in14(r14L), .in15(r15L),
    .out(out_13), .sel(RowSel2));
  Register #(.width(5)) register_1 (.D(num16), .en(in_6), .Q(num16_t), .clk(clk));  // open: clr
  Register #(.width(3)) register_2 (.D(vlen), .en(in_6), .Q(vlen_t), .clk(clk));  // open: clr

  // Other names for the same wires on the sheet: cfg = in_6; RAMhi[31:0] = RAMOutHi; RAMlo[31:0] = RAMOutLo;
  //   rOutHi1[31:0] = out_10; rOutHi2[31:0] = out_11; rOutLo1[31:0] = out_12; rOutLo2[31:0] = out_13
endmodule

module VRegCtrl (
  input  [5:0] vop,
  output [3:0] _16bitRegs,
  output vlen,
  output cfg
);
endmodule

module VTC (
  input  [2:0] vlen,
  input  [4:0] num16,
  input  [4:0] VirtAddr,
  output [7:0] PA
);

  wire is16, islen4, not_1_out;
  wire [1:0] bit_extender_4_out, bit_extender_5_out, priority_encoder_1_out, RegSel;
  wire [2:0] lgvlen;
  wire [3:0] adder_2_out, adder_3_out, demultiplexer_1_out0, shifter_1_out, shifter_2_out;
  wire [7:0] adder_1_out, bit_extender_1_out, multiplexer_1_out, shifter_3_out, shifter_4_out, shifter_5_out,
       vaddr;

  Demultiplexer #(.select(2), .enable("false")) demultiplexer_1 (
    .out0(demultiplexer_1_out0[0]), .out1(demultiplexer_1_out0[1]), .out2(demultiplexer_1_out0[2]),
    .out3(demultiplexer_1_out0[3]), .in(1'b1), .sel(RegSel));
  assign bit_extender_1_out = {{3{1'b0}}, num16};  // Bit_Extender bit_extender_1
  assign {lgvlen[2], islen4, lgvlen[0]} = {{1{1'b0}}, priority_encoder_1_out};  // Bit_Extender bit_extender_2
  Priority_Encoder #(.select(2), .disabled(0)) priority_encoder_1 (
    .in0(vlen[0]), .in1(vlen[1]), .in2(vlen[2]), .out(priority_encoder_1_out));  // open: in3, gs, en_out, en_in
  assign vaddr = {{3{1'b0}}, VirtAddr};  // Bit_Extender bit_extender_3
  assign bit_extender_4_out = {{1{1'b0}}, islen4};  // Bit_Extender bit_extender_4
  assign bit_extender_5_out = {{1{1'b0}}, is16};  // Bit_Extender bit_extender_5
  Adder adder_1 (.a(bit_extender_1_out), .b(vaddr), .out(adder_1_out));  // open: cin, cout
  Comparator comparator_1 (.a(vaddr), .b(bit_extender_1_out), .lt(is16));  // open: gt, eq
  Shifter #(.width(4)) shifter_1 (.in(demultiplexer_1_out0), .\dist (bit_extender_4_out), .out(shifter_1_out));
  Shifter #(.width(4)) shifter_2 (.in(demultiplexer_1_out0), .\dist (bit_extender_5_out), .out(shifter_2_out));
  Shifter shifter_3 (.in(vaddr), .\dist ({lgvlen[2], islen4, lgvlen[0]}), .out(shifter_3_out));
  Adder #(.width(4)) adder_2 (.a(demultiplexer_1_out0), .b(shifter_1_out), .out(adder_2_out));  // open: cin, cout
  Adder #(.width(4)) adder_3 (.a(demultiplexer_1_out0), .b(shifter_2_out), .out(adder_3_out));  // open: cin, cout
  Shifter shifter_4 (.in(shifter_3_out), .\dist (3'b001), .out(shifter_4_out));
  // Probe on {multiplexer_1_out[7], PA[7:4], RegSel, multiplexer_1_out[0]}
  Multiplexer #(.width(8), .enable("false")) multiplexer_1 (
    .in0(shifter_4_out), .in1(shifter_5_out),
    .out({multiplexer_1_out[7], PA[7:4], RegSel, multiplexer_1_out[0]}), .sel(not_1_out));
  Shifter shifter_5 (.in(adder_1_out), .\dist ({lgvlen[2], islen4, lgvlen[0]}), .out(shifter_5_out));
  not not_1 (not_1_out, is16);
  Multiplexer #(.select(2), .width(4), .enable("false")) multiplexer_2 (
    .in0(demultiplexer_1_out0), .in1(adder_2_out), .in2(adder_3_out), .in3(4'b1111), .out(PA[3:0]),
    .sel({is16, islen4}));

  // Other names for the same wires on the sheet: lgvlen[1] = islen4; RowSel[3:0] = PA[7:4]

  // Notes on the sheet:
  //   PA - 4 MSB - RowSel
  //   PA - 4 LSB - RegSetSel
endmodule

module VOF (
  input  [3:0] DSel,
  input  [31:0] InHi,
  input  [31:0] InLo,
  input  is16,
  output [31:0] OutHi,
  output [31:0] OutLo
);

  wire Lo2Hi, multiplexer_5_out, multiplexer_6_out, multiplexer_7_out, multiplexer_8_out, shift, xor_1_out;
  wire [15:0] bit_extender_9_out, bit_extender_10_out, bit_extender_11_out, bit_extender_12_out, HExHi0,
       HExHi16, HExLo0, HExLo16, LExHi0, LExHi16, LExLo0, LExLo16, MaskHi0, MaskHi16, MaskLo0, MaskLo16,
       multiplexer_2_out, multiplexer_3_out, multiplexer_9_out, multiplexer_10_out, multiplexer_11_out,
       multiplexer_12_out;
  wire [31:0] multiplexer_4_out, shifter_1_out;

  assign HExHi16 = {{8{1'b0}}, MaskHi16[15:8]};  // Bit_Extender bit_extender_1
  assign HExHi0 = {{8{1'b0}}, MaskHi16[7:0]};  // Bit_Extender bit_extender_2
  assign HExLo16 = {{8{1'b0}}, MaskHi0[15:8]};  // Bit_Extender bit_extender_3
  assign HExLo0 = {{8{1'b0}}, MaskHi0[7:0]};  // Bit_Extender bit_extender_4
  assign LExHi16 = {{8{1'b0}}, MaskLo16[15:8]};  // Bit_Extender bit_extender_5
  assign LExHi0 = {{8{1'b0}}, MaskLo16[7:0]};  // Bit_Extender bit_extender_6
  assign LExLo16 = {{8{1'b0}}, MaskLo0[15:8]};  // Bit_Extender bit_extender_7
  assign LExLo0 = {{8{1'b0}}, MaskLo0[7:0]};  // Bit_Extender bit_extender_8
  assign bit_extender_9_out = {{15{DSel[3]}}, DSel[3]};  // Bit_Extender bit_extender_9
  assign bit_extender_10_out = {{15{DSel[0]}}, DSel[0]};  // Bit_Extender bit_extender_10
  assign bit_extender_11_out = {{15{DSel[2]}}, DSel[2]};  // Bit_Extender bit_extender_11
  assign bit_extender_12_out = {{15{DSel[1]}}, DSel[1]};  // Bit_Extender bit_extender_12
  assign MaskHi16 = bit_extender_9_out & InHi[31:16];  // AND_Gate and_1, 16 bits wide
  assign MaskHi0 = bit_extender_11_out & InHi[15:0];  // AND_Gate and_2, 16 bits wide
  assign MaskLo16 = bit_extender_12_out & InLo[31:16];  // AND_Gate and_3, 16 bits wide
  assign MaskLo0 = bit_extender_10_out & InLo[15:0];  // AND_Gate and_4, 16 bits wide
  nor nor_1 (Lo2Hi, DSel[3], DSel[2]);
  Multiplexer #(.disabled(0)) multiplexer_1 (.in0(DSel[2]), .in1(DSel[0]), .out(shift), .sel(Lo2Hi), .en(xor_1_out));
  xor xor_1 (xor_1_out, DSel[3], DSel[2], DSel[1], DSel[0]);
  Multiplexer #(.width(16), .enable("false")) multiplexer_2 (
    .in0(MaskHi16), .in1(MaskLo16), .out(multiplexer_2_out), .sel(Lo2Hi));
  Multiplexer #(.width(16), .enable("false")) multiplexer_3 (
    .in0(MaskHi0), .in1(MaskLo0), .out(multiplexer_3_out), .sel(Lo2Hi));
  Shifter #(.width(32)) shifter_1 (.in({multiplexer_2_out, multiplexer_3_out}), .\dist (5'b10000), .out(shifter_1_out));
  // Probe on multiplexer_4_out
  Multiplexer #(.width(32), .enable("false")) multiplexer_4 (
    .in0({multiplexer_2_out, multiplexer_3_out}), .in1(shifter_1_out), .out(multiplexer_4_out), .sel(shift));
  Multiplexer #(.enable("false")) multiplexer_5 (.out(multiplexer_5_out), .sel(is16));  // open: in0, in1
  Multiplexer #(.enable("false")) multiplexer_6 (.out(multiplexer_6_out), .sel(is16));  // open: in0, in1
  Multiplexer #(.enable("false")) multiplexer_7 (.out(multiplexer_7_out), .sel(is16));  // open: in0, in1
  Multiplexer #(.enable("false")) multiplexer_8 (.out(multiplexer_8_out), .sel(is16));  // open: in0, in1
  Multiplexer #(.width(16), .enable("false")) multiplexer_9 (
    .in0(HExHi16), .in1(HExLo16), .out(multiplexer_9_out), .sel(Lo2Hi));
  Multiplexer #(.width(16), .enable("false")) multiplexer_10 (
    .in0(HExHi0), .in1(HExLo0), .out(multiplexer_10_out), .sel(Lo2Hi));
  Multiplexer #(.width(16), .enable("false")) multiplexer_11 (
    .in0(LExHi16), .in1(LExLo16), .out(multiplexer_11_out), .sel(Lo2Hi));
  Multiplexer #(.width(16), .enable("false")) multiplexer_12 (
    .in0(LExHi0), .in1(LExLo0), .out(multiplexer_12_out), .sel(Lo2Hi));
  // Probe on {multiplexer_9_out, multiplexer_10_out}
  // Probe on {multiplexer_11_out, multiplexer_12_out}

  // Other names for the same wires on the sheet: DSel4[3:0] = DSel; InHi0[15:0] = InHi[15:0];
  //   InHi16[15:0] = InHi[31:16]; InLo0[15:0] = InLo[15:0]; InLo16[15:0] = InLo[31:16]

  // Notes on the sheet:
  //   Vector Output Format
  //   8-bit Extend
  //   Bit Expand DSel4
  //   Mask
  //   Mux/Extend 8 bit
  //   Mux To OutHi/OutLo
endmodule
